# Fritzing sketch diagram (saved by Fritzing 0.9.3b)
breadboards: 1

parts:
  J1 = Piezo Speaker
  Part1 = Photon
  Part2 = Tri-Axis Gyro Breakout - L3G4200D
  Part3 = Adafruit 1.44 inch TFT Breakout [part_number="Adafruit #2088"]
  SONAR1 = Maxbotix MaxSonar Ultrasonic Sensor
  S1 = Momentary Switch [package=ksa_sealed_tac_switch]  # not connected

nets:
  GND: J1.pin1, Part1.GND, Part2.GND, Part3.GND, SONAR1.GND
  N1: J1.pin2, Part1.D7
  N2: Part1.A1, Part3.TFTCS
  N3: Part1.A2, Part3.RESET
  N4: Part1.A3, Part3.SCK
  N5: Part1.A4, Part3.MISO
  N6: Part1.A5, Part3.MOSI
  VIN: Part1.VIN, Part2.VCC, Part3.VIN, SONAR1.+5V
  N7: Part1.D0, Part2.SDA
  N8: Part1.D1, Part2.SCL
  N9: Part1.D3, SONAR1.PW

custom parts:
  Adafruit 1.44 inch TFT Breakout: This lovely little display breakout is the best way to add a small, colorful and bright display to any project. Since the display uses 4-wire SPI to communicate and has its own pixel-addressable frame buffer, it can be used with every kind of microcontroller. Even a very small one with low memory and few pins available! The 1.44" display has 128x128 color pixels. Unlike the low cost "Nokia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
  Maxbotix MaxSonar Ultrasonic Sensor: Maxbotix MaxSonar Ultrasonic Sensor LV-EZ0, LV-EZ1, LV-EZ2, LV-EZ3, LV-EZ4
